# Fritzing sketch fade-led-pwm (saved by Fritzing 0.9.3b)
breadboards: 1

parts:
  R1 = Resistor [tolerance=±5% resistance=470 package=THT]
  LED1 = LED - 5mm [color="Red (633nm)" package="5 mm [THT]"]
  Part1 = Arduino Uno (Rev3) - ICSP

nets:
  N1: R1.Pin_0, Part1.D12/MISO
  N2: R1.Pin_1, LED1.anode
  N3: LED1.cathode, Part1.GND
