# Fritzing sketch potmeter (saved by Fritzing 0.9.3b)
breadboards: 1

parts:
  Part2 = Arduino Uno (Rev3) - ICSP
  R1 = Rotary Potentiometer (Small) [maximum_resistance=100kΩ package=THT]

nets:
  N1: Part2.A2, R1.wiper
  N2: Part2.5V, R1.leg1
  N3: Part2.GND, R1.leg2
