# Fritzing sketch ultrasoon-sensor-HC-SR04 (saved by Fritzing 0.9.3b)
breadboards: 1

parts:
  Part2 = Arduino Uno (Rev3) - ICSP
  hc-sr1 = hc-sr04

nets:
  N1: Part2.D8, hc-sr1.Echo
  N2: Part2.D12/MISO, hc-sr1.Trig
  5V: Part2.5V, hc-sr1.VCC
  GND: Part2.GND, hc-sr1.GND
