# Fritzing sketch analoge-ps2-joystick (saved by Fritzing 0.9.3b)

parts:
  Part2 = Arduino Uno (Rev3) - ICSP
  Part3 = Thumb Joystick

nets:
  N1: Part2.A0, Part3.VERT
  N2: Part2.A5/SCL, Part3.HORZ
  N3: Part2.D12/MISO, Part3.SEL
  5V: Part2.5V, Part3.VCC
  GND: Part2.GND, Part3.GND

notes:
  WARNING: Pin layout differs from video
