# Fritzing sketch ir-receiver (saved by Fritzing 0.9.3b)
breadboards: 1

parts:
  Part2 = Arduino Uno (Rev3) - ICSP
  IR1 = TSOP312.., 314.. [package=THT]

nets:
  N1: Part2.D12/MISO, IR1.Data
  N2: Part2.3V3, IR1.Vs
  GND: Part2.GND, IR1.GND
