# Fritzing sketch dht11-dht22 (saved by Fritzing 0.9.3b)
breadboards: 1

parts:
  Part2 = Arduino Uno (Rev3) - ICSP
  RHT1 = Humidity and Temperature Sensor RHT03

nets:
  N1: Part2.D12/MISO, RHT1.Data-signal
  3V3: Part2.3V3, RHT1.Vcc
  N2: Part2.GND, RHT1.GND_2
