# Fritzing sketch E15-switch-long-press (saved by Fritzing 0.9.3b)
breadboards: 1

parts:
  Part2 = Arduino Uno (Rev3) - ICSP
  S1 = Pushbutton [package="[THT]"]
  R1 = Resistor [tolerance=±5% resistance=100 package=THT]

nets:
  N1: Part2.5V, S1.Pin_3, S1.Pin_4
  N2: Part2.D12/MISO, S1.Pin_1, S1.Pin_2, R1.Pin_0
  N3: Part2.GND, R1.Pin_1
