# Fritzing sketch LCD-SPI-ST7920-128x64 (saved by Fritzing 0.9.3b)
breadboards: 1

parts:
  Part2 = Arduino Uno (Rev3) - ICSP
  GLCD_128x1 = 128 x 64 Graphic LCD

nets:
  N1: Part2.D10_PWM/SS, GLCD_128x1.4_D/I
  N2: Part2.D11_PWM/MOSI, GLCD_128x1.5_R/W
  N3: Part2.D13/SCK, GLCD_128x1.6_Enable
  N4: Part2.3V3, GLCD_128x1.19_A(+)
  N5: Part2.5V, GLCD_128x1.2_Vdd
  N6: Part2.GND, GLCD_128x1.1_Vss, GLCD_128x1.15_CS1, GLCD_128x1.20_K(-)
