# Fritzing sketch OLED-I2C-SSD1306-128X64 (saved by Fritzing 0.9.3b)

parts:
  Part2 = Arduino Uno (Rev3) - ICSP
  Grove1 = Grove OLED 128x96

nets:
  N1: Part2.A4/SDA, Grove1.SDA
  N2: Part2.A5/SCL, Grove1.SCL
  3V3: Part2.3V3, Grove1.VCC
  GND: Part2.GND, Grove1.GND
