# Fritzing sketch LDR (saved by Fritzing 0.9.3b)
breadboards: 1

parts:
  R1 = Resistor [tolerance=±5% resistance=1k package=THT]
  Part1 = Arduino Uno (Rev3) - ICSP
  R2 = Photocell (LDR) [package=THT]

nets:
  N1: R1.Pin_0, Part1.A0, R2.pin_1
  N2: R1.Pin_1, Part1.GND
  N3: Part1.5V, R2.pin_0
