# Fritzing sketch HC-S501-pir-motion-sensor (saved by Fritzing 0.9.3b)

parts:
  Part1 = Arduino Uno (Rev3) - ICSP
  Composant2 = HC-SR501 Body Sensor Module

nets:
  N1: Part1.D12/MISO, Composant2.GND
  5V: Part1.5V, Composant2.VCC
  N2: Part1.GND, Composant2.OUT

custom parts:
  HC-SR501 Body Sensor Module: Pyroelectric Infrared PIR Motion Sensor Detector Module
