# Fritzing sketch slide-potentiometer (saved by Fritzing 0.9.3b)

parts:
  Part1 = Arduino Uno (Rev3) - ICSP
  R3 = Slide Potentiometer [maximum_resistance=100kΩ]

nets:
  N1: Part1.A0, R3.leg1
  N2: Part1.5V, R3.leg2
  N3: Part1.GND, R3.wiper

notes:
  OTB
  GND
  VCC
