# Fritzing sketch SG90-tower-pro-servo (saved by Fritzing 0.9.3b)
breadboards: 1

parts:
  Part1 = Arduino Uno (Rev3) - ICSP
  J2 = Basic Servo

nets:
  N1: Part1.D8, J2.pulse
  GND: Part1.GND, J2.gnd
