# Fritzing sketch E26-4x4-membrane-keypad (saved by Fritzing 0.9.4)

parts:
  Part2 = Arduino Uno (Rev3) - ICSP
  Keypad4x2 = Keypad Membran 4x4

nets:
  N1: Part2.D8, Keypad4x2.Pin2
  N2: Part2.D9_PWM, Keypad4x2.Pin1
  N3: Part2.D2, Keypad4x2.Pin8
  N4: Part2.D3_PWM, Keypad4x2.Pin7
  N5: Part2.D4, Keypad4x2.Pin6
  N6: Part2.D5_PWM, Keypad4x2.Pin5
  N7: Part2.D6_PWM, Keypad4x2.Pin4
  N8: Part2.D7, Keypad4x2.Pin3

custom parts:
  Keypad Membran 4x4: Membrane Keypad 4x4 Matrix
