# Fritzing sketch E28-touch-sensor (saved by Fritzing 0.9.4)

parts:
  TTP223B2 = TTP223B Capacitive Touch Sensor Module
  Part2 = Arduino Uno (Rev3) - ICSP

nets:
  GND: TTP223B2.GND, Part2.GND
  VCC: TTP223B2.VCC, Part2.5V
  N1: TTP223B2.SIG, Part2.D8

custom parts:
  TTP223B Capacitive Touch Sensor Module: The TTP223B capacitive touch sensor module uses the TTP223B IC. The appropriate voltage is approximately 2 to 5.5 volts.
