# Fritzing sketch i2c-lcd-ultrasoon-challenge (saved by Fritzing 0.9.3b)
breadboards: 1

parts:
  hc-sr1 = hc-sr04
  Part1 = Arduino Uno (Rev3) - ICSP
  LCD1 = LCD screen  # not connected

nets:
  VCC: hc-sr1.VCC, Part1.5V
  N1: hc-sr1.Trig, Part1.D12/MISO
  N2: hc-sr1.Echo, Part1.D8
  GND: hc-sr1.GND, Part1.GND

notes:
  SDA
  SCL
  GND
  Vcc
